// Logisim project Single_Cycle_CPU.circ as structural Verilog: 1 circuit, main circuit main
module main (
);

  wire Clk, clock_1_out, Halt;

  Multiplexer multiplexer_1 (.in0(clock_1_out), .in1(1'b0), .out(Clk), .sel(Halt));
  Clock clock_1 (.out(clock_1_out));
  // control_unit control_unit_1: pin names not known
  // CP0 cp0_1: pin names not known
endmodule
